// Logisim project ASSINGMENT 1.circ as structural Verilog: 4 circuits, main circuit main
module main (
  input  A__Fan,
  input  B__Bulb1,
  input  C__Bulb2,
  input  D__Bulb3,
  output F__Switch
);

  wire ic_4072_4_input_or_gate_1_out_10, ic_7404_not_gate_1_out_7, ic_7404_not_gate_1_out_8,
       ic_7404_not_gate_1_out_9, ic_7421_4_input_and_gate_1_out_9, ic_7421_4_input_and_gate_1_out_10,
       ic_7421_4_input_and_gate_2_out_9, ic_7421_4_input_and_gate_2_out_10, ic_7421_4_input_and_gate_3_out_9,
       ic_7421_4_input_and_gate_3_out_10;

  IC_7404__NOT_gate ic_7404_not_gate_1 (
    .in_1(D__Bulb3), .in_2(C__Bulb2), .in_3(B__Bulb1), .out_7(ic_7404_not_gate_1_out_7),
    .out_8(ic_7404_not_gate_1_out_8), .out_9(ic_7404_not_gate_1_out_9));  // open: in_4, in_5, in_6, out_10, out_11, out_12
  IC_7421__4_input_AND_gate ic_7421_4_input_and_gate_1 (
    .in_1(A__Fan), .in_2(ic_7404_not_gate_1_out_9), .in_3(C__Bulb2), .in_4(ic_7404_not_gate_1_out_7),
    .in_5(D__Bulb3), .in_6(ic_7404_not_gate_1_out_8), .in_7(ic_7404_not_gate_1_out_9), .in_8(A__Fan),
    .out_9(ic_7421_4_input_and_gate_1_out_9), .out_10(ic_7421_4_input_and_gate_1_out_10));
  IC_7421__4_input_AND_gate ic_7421_4_input_and_gate_2 (
    .in_1(A__Fan), .in_2(B__Bulb1), .in_3(ic_7404_not_gate_1_out_8), .in_4(ic_7404_not_gate_1_out_8),
    .in_5(D__Bulb3), .in_6(C__Bulb2), .in_7(ic_7404_not_gate_1_out_9), .in_8(A__Fan),
    .out_9(ic_7421_4_input_and_gate_2_out_9), .out_10(ic_7421_4_input_and_gate_2_out_10));
  IC_7421__4_input_AND_gate ic_7421_4_input_and_gate_3 (
    .in_1(A__Fan), .in_2(A__Fan), .in_3(C__Bulb2), .in_4(ic_7404_not_gate_1_out_7), .in_5(D__Bulb3),
    .in_6(ic_7404_not_gate_1_out_8), .in_7(A__Fan), .in_8(A__Fan), .out_9(ic_7421_4_input_and_gate_3_out_9),
    .out_10(ic_7421_4_input_and_gate_3_out_10));
  IC_4072__4_input_OR_gate ic_4072_4_input_or_gate_1 (
    .in_1(ic_4072_4_input_or_gate_1_out_10), .in_2(ic_4072_4_input_or_gate_1_out_10),
    .in_3(ic_7421_4_input_and_gate_1_out_9), .in_4(ic_7421_4_input_and_gate_1_out_10),
    .in_5(ic_7421_4_input_and_gate_2_out_10), .in_6(ic_7421_4_input_and_gate_2_out_9),
    .in_7(ic_7421_4_input_and_gate_3_out_10), .in_8(ic_7421_4_input_and_gate_3_out_9), .out_9(F__Switch),
    .out_10(ic_4072_4_input_or_gate_1_out_10));
endmodule

module IC_4072__4_input_OR_gate (
  input  in_1,
  input  in_2,
  input  in_3,
  input  in_4,
  input  in_5,
  input  in_6,
  input  in_7,
  input  in_8,
  output out_9,
  output out_10
);

  or or_1 (out_9, in_1, in_2, in_3, in_4);
  or or_2 (out_10, in_5, in_6, in_7, in_8);
endmodule

module IC_7421__4_input_AND_gate (
  input  in_1,
  input  in_2,
  input  in_3,
  input  in_4,
  input  in_5,
  input  in_6,
  input  in_7,
  input  in_8,
  output out_9,
  output out_10
);

  and and_1 (out_9, in_1, in_2, in_3, in_4);
  and and_2 (out_10, in_5, in_6, in_7, in_8);
endmodule

module IC_7404__NOT_gate (
  input  in_1,
  input  in_2,
  input  in_3,
  input  in_4,
  input  in_5,
  input  in_6,
  output out_7,
  output out_8,
  output out_9,
  output out_10,
  output out_11,
  output out_12
);

  not not_1 (out_7, in_1);
  not not_2 (out_8, in_2);
  not not_3 (out_9, in_3);
  not not_4 (out_10, in_4);
  not not_5 (out_11, in_5);
  not not_6 (out_12, in_6);
endmodule
