// Logisim project Sequential Circuit using JK Flip-Flops.circ as structural Verilog: 3 circuits, main circuit main
module main (
  input  X,
  output Q1,
  output Q2
);

  wire CLK_out, ic_7486_1_out_11;

  IC_7486 ic_7486_1 (
    .in_5(Q2), .in_6(X), .out_11(ic_7486_1_out_11));  // open: in_1, in_2, in_3, in_4, in_7, in_8, out_9, out_10, out_12
  IC_74107 ic_74107_1 (
    .in_1(ic_7486_1_out_11), .in_2(ic_7486_1_out_11), .in_3(1'b1), .in_4(1'b1), .in_5(CLK_out), .out_6(Q1),
    .out_8(Q2));  // open: out_7, out_9
  Clock CLK (.out(CLK_out));
endmodule

module IC_7486 (
  input  in_1,
  input  in_2,
  input  in_3,
  input  in_4,
  input  in_5,
  input  in_6,
  input  in_7,
  input  in_8,
  output out_9,
  output out_10,
  output out_11,
  output out_12
);

  xor xor_1 (out_9, in_1, in_2);
  xor xor_2 (out_10, in_3, in_4);
  xor xor_3 (out_11, in_5, in_6);
  xor xor_4 (out_12, in_7, in_8);
endmodule

module IC_74107 (
  input  in_1,
  input  in_2,
  input  in_3,
  input  in_4,
  input  in_5,
  output out_6,
  output out_7,
  output out_8,
  output out_9
);

  J_K_Flip_Flop j_k_ff_1 (.J(in_1), .clk(in_5), .K(in_2), .Q(out_6), .Qn(out_7));  // open: preset, en, reset
  J_K_Flip_Flop j_k_ff_2 (.J(in_3), .clk(in_5), .K(in_4), .Q(out_8), .Qn(out_9));  // open: preset, en, reset
endmodule
