// Logisim project Sequential Circuit using T Flip-Flops.circ as structural Verilog: 3 circuits, main circuit main
module main (
  input  X,
  output Q1,
  output Q2
);

  wire CLK_out, ic_7486_1_out_11;

  IC_7486 ic_7486_1 (
    .in_5(Q2), .in_6(X), .out_11(ic_7486_1_out_11));  // open: in_1, in_2, in_3, in_4, in_7, in_8, out_9, out_10, out_12
  IC_7474 ic_7474_1 (
    .in_1(ic_7486_1_out_11), .in_2(1'b1), .in_3(CLK_out), .out_4(Q1), .out_6(Q2));  // open: out_5, out_7
  Clock CLK (.out(CLK_out));
endmodule

module IC_7486 (
  input  in_1,
  input  in_2,
  input  in_3,
  input  in_4,
  input  in_5,
  input  in_6,
  input  in_7,
  input  in_8,
  output out_9,
  output out_10,
  output out_11,
  output out_12
);

  xor xor_1 (out_9, in_1, in_2);
  xor xor_2 (out_10, in_3, in_4);
  xor xor_3 (out_11, in_5, in_6);
  xor xor_4 (out_12, in_7, in_8);
endmodule

module IC_7474 (
  input  in_1,
  input  in_2,
  input  in_3,
  output out_4,
  output out_5,
  output out_6,
  output out_7
);

  T_Flip_Flop t_ff_1 (.clk(in_3), .T(in_1), .Q(out_4), .Qn(out_5));  // open: preset, reset, en
  T_Flip_Flop t_ff_2 (.clk(in_3), .T(in_2), .Q(out_6), .Qn(out_7));  // open: preset, reset, en
endmodule
