// Logisim project Full Adder using Multiplexer.circ as structural Verilog: 3 circuits, main circuit main
module main (
  input  A,
  input  B,
  input  Cin,
  output Sum,
  output Carry
);

  wire ic_7404_1_out_11;

  IC_7404 ic_7404_1 (
    .in_5(A), .out_11(ic_7404_1_out_11));  // open: in_1, in_2, in_3, in_4, in_6, out_7, out_8, out_9, out_10, out_12
  _4_1_Mux u_4_1_mux_1 (.I0(A), .I1(ic_7404_1_out_11), .I2(ic_7404_1_out_11), .I3(A), .Y(Sum), .S1(B), .S0(Cin));
  _4_1_Mux u_4_1_mux_2 (.I0(1'b0), .I1(A), .I2(A), .I3(1'b1), .Y(Carry), .S1(B), .S0(Cin));
endmodule

module _4_1_Mux (
  input  I0,
  input  I1,
  input  I2,
  input  I3,
  input  S1,
  input  S0,
  output Y
);

  wire and_1_out, and_2_out, and_3_out, and_4_out, not_1_out, not_2_out;

  not not_1 (not_1_out, S1);
  not not_2 (not_2_out, S0);
  and and_1 (and_1_out, I0, not_1_out, not_2_out);
  and and_2 (and_2_out, I1, not_1_out, S0);
  and and_3 (and_3_out, I2, S1, not_2_out);
  and and_4 (and_4_out, I3, S1, S0);
  or or_1 (Y, and_1_out, and_2_out, and_3_out, and_4_out);
endmodule

module IC_7404 (
  input  in_1,
  input  in_2,
  input  in_3,
  input  in_4,
  input  in_5,
  input  in_6,
  output out_7,
  output out_8,
  output out_9,
  output out_10,
  output out_11,
  output out_12
);

  not not_1 (out_7, in_1);
  not not_2 (out_8, in_2);
  not not_3 (out_9, in_3);
  not not_4 (out_10, in_4);
  not not_5 (out_11, in_5);
  not not_6 (out_12, in_6);
endmodule
