// Logisim project XOR & XNOR Gate using IC 7400 (NAND Gate).circ as structural Verilog: 2 circuits, main circuit main
module main (
  input  A,
  input  B,
  output XOR_Gate_Output,
  output XNOR_Gate_Output
);

  wire ic_7400_1_out_9, ic_7400_1_out_10, ic_7400_1_out_11, ic_7400_2_out_9, ic_7400_2_out_10,
       ic_7400_2_out_11, ic_7400_2_out_12;

  ic_7400 ic_7400_1 (
    .in_1(ic_7400_1_out_11), .in_2(B), .in_3(ic_7400_1_out_11), .in_4(A), .in_5(B), .in_6(A),
    .in_7(ic_7400_1_out_10), .in_8(ic_7400_1_out_9), .out_9(ic_7400_1_out_9), .out_10(ic_7400_1_out_10),
    .out_11(ic_7400_1_out_11), .out_12(XOR_Gate_Output));
  ic_7400 ic_7400_2 (
    .in_1(ic_7400_2_out_11), .in_2(A), .in_3(ic_7400_2_out_11), .in_4(B), .in_5(B), .in_6(A),
    .in_7(ic_7400_2_out_10), .in_8(ic_7400_2_out_9), .out_9(ic_7400_2_out_9), .out_10(ic_7400_2_out_10),
    .out_11(ic_7400_2_out_11), .out_12(ic_7400_2_out_12));
  ic_7400 ic_7400_3 (
    .in_3(ic_7400_2_out_12), .in_4(ic_7400_2_out_12), .out_10(XNOR_Gate_Output));  // open: in_1, in_2, in_5, in_6, in_7, in_8, out_9, out_11, out_12
endmodule

module ic_7400 (
  input  in_1,
  input  in_2,
  input  in_3,
  input  in_4,
  input  in_5,
  input  in_6,
  input  in_7,
  input  in_8,
  output out_9,
  output out_10,
  output out_11,
  output out_12
);

  nand nand_1 (out_9, in_1, in_2);
  nand nand_2 (out_10, in_3, in_4);
  nand nand_3 (out_11, in_5, in_6);
  nand nand_4 (out_12, in_7, in_8);
endmodule
