// Logisim project XOR & XNOR Gate using IC 7402 (NOR Gate).circ as structural Verilog: 2 circuits, main circuit main
module main (
  input  A,
  input  B,
  output XNOR_Gate_Output,
  output XOR_Gate_Output
);

  wire ic_7402_1_out_10, ic_7402_1_out_11, ic_7402_1_out_12, ic_7402_2_out_9, ic_7402_2_out_10,
       ic_7402_2_out_11, ic_7402_2_out_12;

  ic_7402 ic_7402_1 (
    .in_1(ic_7402_1_out_12), .in_2(ic_7402_1_out_10), .in_3(B), .in_4(ic_7402_1_out_11), .in_5(B), .in_6(A),
    .in_7(ic_7402_1_out_11), .in_8(A), .out_9(XNOR_Gate_Output), .out_10(ic_7402_1_out_10),
    .out_11(ic_7402_1_out_11), .out_12(ic_7402_1_out_12));
  ic_7402 ic_7402_2 (
    .in_1(ic_7402_2_out_12), .in_2(ic_7402_2_out_10), .in_3(A), .in_4(ic_7402_2_out_11), .in_5(B), .in_6(A),
    .in_7(ic_7402_2_out_11), .in_8(A), .out_9(ic_7402_2_out_9), .out_10(ic_7402_2_out_10),
    .out_11(ic_7402_2_out_11), .out_12(ic_7402_2_out_12));
  ic_7402 ic_7402_3 (
    .in_3(ic_7402_2_out_9), .in_4(ic_7402_2_out_9), .out_10(XOR_Gate_Output));  // open: in_1, in_2, in_5, in_6, in_7, in_8, out_9, out_11, out_12
endmodule

module ic_7402 (
  input  in_1,
  input  in_2,
  input  in_3,
  input  in_4,
  input  in_5,
  input  in_6,
  input  in_7,
  input  in_8,
  output out_9,
  output out_10,
  output out_11,
  output out_12
);

  nor nor_1 (out_9, in_1, in_2);
  nor nor_2 (out_10, in_3, in_4);
  nor nor_3 (out_11, in_5, in_6);
  nor nor_4 (out_12, in_7, in_8);
endmodule
