// Logisim project Minterms & Maxterms Using IC 7411, IC 4075, IC 7404 (LAB 3).circ as structural Verilog: 4 circuits, main circuit main
module main (
  input  A,
  input  B,
  input  C,
  output MINTERMS,
  output MAXTERMS
);

  wire ic_4075_or_gate_1_out_10, ic_4075_or_gate_1_out_11, ic_4075_or_gate_1_out_12,
       ic_4075_or_gate_2_out_11, ic_4075_or_gate_2_out_12, ic_7404_not_gate_1_out_7,
       ic_7404_not_gate_1_out_8, ic_7404_not_gate_1_out_9, ic_7411_and_gate_1_out_10,
       ic_7411_and_gate_1_out_11, ic_7411_and_gate_1_out_12, ic_7411_and_gate_2_out_12;

  IC_7404_NOT_GATE ic_7404_not_gate_1 (
    .in_1(C), .in_2(B), .in_3(A), .out_7(ic_7404_not_gate_1_out_7), .out_8(ic_7404_not_gate_1_out_8),
    .out_9(ic_7404_not_gate_1_out_9));  // open: in_4, in_5, in_6, out_10, out_11, out_12
  IC_7411_AND_GATE ic_7411_and_gate_1 (
    .in_1(ic_7404_not_gate_1_out_9), .in_2(ic_7404_not_gate_1_out_7), .in_3(B), .in_4(A), .in_5(B),
    .in_6(ic_7404_not_gate_1_out_7), .in_7(ic_7404_not_gate_1_out_9), .in_8(ic_7404_not_gate_1_out_8),
    .in_9(C), .out_10(ic_7411_and_gate_1_out_10), .out_11(ic_7411_and_gate_1_out_11),
    .out_12(ic_7411_and_gate_1_out_12));
  IC_4075_OR_GATE ic_4075_or_gate_1 (
    .in_1(ic_7404_not_gate_1_out_8), .in_2(ic_7404_not_gate_1_out_7), .in_3(A), .in_4(B), .in_5(C),
    .in_6(ic_7404_not_gate_1_out_9), .in_7(A), .in_8(C), .in_9(B), .out_10(ic_4075_or_gate_1_out_10),
    .out_11(ic_4075_or_gate_1_out_11), .out_12(ic_4075_or_gate_1_out_12));
  IC_4075_OR_GATE ic_4075_or_gate_2 (
    .in_4(ic_7404_not_gate_1_out_7), .in_5(ic_7404_not_gate_1_out_8), .in_6(ic_7404_not_gate_1_out_9),
    .in_7(ic_7404_not_gate_1_out_9), .in_8(ic_7404_not_gate_1_out_7), .in_9(B),
    .out_11(ic_4075_or_gate_2_out_11), .out_12(ic_4075_or_gate_2_out_12));  // open: in_1, in_2, in_3, out_10
  IC_4075_OR_GATE ic_4075_or_gate_3 (
    .in_7(ic_7411_and_gate_1_out_10), .in_8(ic_7411_and_gate_1_out_11), .in_9(ic_7411_and_gate_1_out_12),
    .out_12(MINTERMS));  // open: in_1, in_2, in_3, in_4, in_5, in_6, out_10, out_11
  IC_7411_AND_GATE ic_7411_and_gate_2 (
    .in_4(ic_4075_or_gate_2_out_12), .in_5(ic_4075_or_gate_2_out_11), .in_6(ic_7411_and_gate_2_out_12),
    .in_7(ic_4075_or_gate_1_out_10), .in_8(ic_4075_or_gate_1_out_11), .in_9(ic_4075_or_gate_1_out_12),
    .out_11(MAXTERMS), .out_12(ic_7411_and_gate_2_out_12));  // open: in_1, in_2, in_3, out_10

  // Notes on the sheet:
  //   A
  //   A'
  //   B
  //   C
  //   B'
  //   C'
endmodule

module IC_7411_AND_GATE (
  input  in_1,
  input  in_2,
  input  in_3,
  input  in_4,
  input  in_5,
  input  in_6,
  input  in_7,
  input  in_8,
  input  in_9,
  output out_10,
  output out_11,
  output out_12
);

  and and_1 (out_10, in_1, in_2, in_3);
  and and_2 (out_11, in_4, in_5, in_6);
  and and_3 (out_12, in_7, in_8, in_9);
endmodule

module IC_4075_OR_GATE (
  input  in_1,
  input  in_2,
  input  in_3,
  input  in_4,
  input  in_5,
  input  in_6,
  input  in_7,
  input  in_8,
  input  in_9,
  output out_10,
  output out_11,
  output out_12
);

  or or_1 (out_10, in_1, in_2, in_3);
  or or_2 (out_11, in_4, in_5, in_6);
  or or_3 (out_12, in_7, in_8, in_9);
endmodule

module IC_7404_NOT_GATE (
  input  in_1,
  input  in_2,
  input  in_3,
  input  in_4,
  input  in_5,
  input  in_6,
  output out_7,
  output out_8,
  output out_9,
  output out_10,
  output out_11,
  output out_12
);

  not not_1 (out_7, in_1);
  not not_2 (out_8, in_2);
  not not_3 (out_9, in_3);
  not not_4 (out_10, in_4);
  not not_5 (out_11, in_5);
  not not_6 (out_12, in_6);
endmodule
