// Logisim project BCD To Excess-3 Converter (Lab 04).circ as structural Verilog: 4 circuits, main circuit main
module main (
  input  W,
  input  X,
  input  Y,
  input  Z,
  output A,
  output B,
  output C,
  output D
);

  wire ic_7404_not_gate_1_out_8, ic_7404_not_gate_1_out_9, ic_7408_and_gate_1_out_9,
       ic_7408_and_gate_1_out_10, ic_7408_and_gate_1_out_11, ic_7408_and_gate_1_out_12,
       ic_7408_and_gate_2_out_9, ic_7408_and_gate_2_out_10, ic_7408_and_gate_2_out_11,
       ic_7408_and_gate_2_out_12, ic_7432_or_gate_1_out_9, ic_7432_or_gate_1_out_12;

  IC_7404__NOT_GATE ic_7404_not_gate_1 (
    .in_1(Z), .in_2(Y), .in_3(X), .out_7(D), .out_8(ic_7404_not_gate_1_out_8),
    .out_9(ic_7404_not_gate_1_out_9));  // open: in_4, in_5, in_6, out_10, out_11, out_12
  IC_7408__AND_GATE ic_7408_and_gate_1 (
    .in_1(ic_7404_not_gate_1_out_8), .in_2(D), .in_3(ic_7408_and_gate_1_out_9), .in_4(X), .in_5(Y), .in_6(X),
    .in_7(Z), .in_8(X), .out_9(ic_7408_and_gate_1_out_9), .out_10(ic_7408_and_gate_1_out_10),
    .out_11(ic_7408_and_gate_1_out_11), .out_12(ic_7408_and_gate_1_out_12));
  IC_7408__AND_GATE ic_7408_and_gate_2 (
    .in_1(Y), .in_2(Z), .in_3(ic_7404_not_gate_1_out_8), .in_4(D), .in_5(Z), .in_6(ic_7404_not_gate_1_out_9),
    .in_7(Y), .in_8(ic_7404_not_gate_1_out_9), .out_9(ic_7408_and_gate_2_out_9),
    .out_10(ic_7408_and_gate_2_out_10), .out_11(ic_7408_and_gate_2_out_11), .out_12(ic_7408_and_gate_2_out_12));
  IC_7432__OR_GATE ic_7432_or_gate_1 (
    .in_1(ic_7408_and_gate_2_out_12), .in_2(ic_7408_and_gate_2_out_11), .in_3(ic_7432_or_gate_1_out_9),
    .in_4(ic_7408_and_gate_1_out_10), .in_5(W), .in_6(ic_7432_or_gate_1_out_12),
    .in_7(ic_7408_and_gate_1_out_11), .in_8(ic_7408_and_gate_1_out_12), .out_9(ic_7432_or_gate_1_out_9),
    .out_10(B), .out_11(A), .out_12(ic_7432_or_gate_1_out_12));
  IC_7432__OR_GATE ic_7432_or_gate_2 (
    .in_5(ic_7408_and_gate_2_out_10), .in_6(ic_7408_and_gate_2_out_9), .out_11(C));  // open: in_1, in_2, in_3, in_4, in_7, in_8, out_9, out_10, out_12
endmodule

module IC_7408__AND_GATE (
  input  in_1,
  input  in_2,
  input  in_3,
  input  in_4,
  input  in_5,
  input  in_6,
  input  in_7,
  input  in_8,
  output out_9,
  output out_10,
  output out_11,
  output out_12
);

  and and_1 (out_9, in_1, in_2);
  and and_2 (out_10, in_3, in_4);
  and and_3 (out_11, in_5, in_6);
  and and_4 (out_12, in_7, in_8);
endmodule

module IC_7432__OR_GATE (
  input  in_1,
  input  in_2,
  input  in_3,
  input  in_4,
  input  in_5,
  input  in_6,
  input  in_7,
  input  in_8,
  output out_9,
  output out_10,
  output out_11,
  output out_12
);

  or or_1 (out_9, in_1, in_2);
  or or_2 (out_10, in_3, in_4);
  or or_3 (out_11, in_5, in_6);
  or or_4 (out_12, in_7, in_8);
endmodule

module IC_7404__NOT_GATE (
  input  in_1,
  input  in_2,
  input  in_3,
  input  in_4,
  input  in_5,
  input  in_6,
  output out_7,
  output out_8,
  output out_9,
  output out_10,
  output out_11,
  output out_12
);

  not not_1 (out_7, in_1);
  not not_2 (out_8, in_2);
  not not_3 (out_9, in_3);
  not not_4 (out_10, in_4);
  not not_5 (out_11, in_5);
  not not_6 (out_12, in_6);
endmodule
