// Logisim project Binary Arithmetic.circ as structural Verilog: 7 circuits, main circuit BCD Adder Circuit
module IC_7432_quadruple_2_Input_OR_gates (
  input  in_1,
  input  in_2,
  input  in_3,
  input  in_4,
  input  in_5,
  input  in_6,
  input  in_7,
  input  in_8,
  output out_9,
  output out_10,
  output out_11,
  output out_12
);

  or or_1 (out_9, in_1, in_2);
  or or_2 (out_10, in_3, in_4);
  or or_3 (out_11, in_5, in_6);
  or or_4 (out_12, in_7, in_8);
endmodule

module IC_7408_quadruple_2_Input_AND_gates (
  input  in_1,
  input  in_2,
  input  in_3,
  input  in_4,
  input  in_5,
  input  in_6,
  input  in_7,
  input  in_8,
  output out_9,
  output out_10,
  output out_11,
  output out_12
);

  and and_1 (out_9, in_1, in_2);
  and and_2 (out_10, in_3, in_4);
  and and_3 (out_11, in_5, in_6);
  and and_4 (out_12, in_7, in_8);
endmodule

module IC_7486_quadruple_2_input_XOR_gates (
  input  in_1,
  input  in_2,
  input  in_3,
  input  in_4,
  input  in_5,
  input  in_6,
  input  in_7,
  input  in_8,
  output out_9,
  output out_10,
  output out_11,
  output out_12
);

  xor xor_1 (out_9, in_1, in_2);
  xor xor_2 (out_10, in_3, in_4);
  xor xor_3 (out_11, in_5, in_6);
  xor xor_4 (out_12, in_7, in_8);
endmodule

module IC_74283_4_bit_binary_adder__Vertical (
  input  Cin,
  input  A1,
  input  B1,
  input  A2,
  input  B2,
  input  A3,
  input  B3,
  input  A4,
  input  B4,
  output S1,
  output S2,
  output S3,
  output S4,
  output Cout
);

  wire adder_1_cout, adder_2_cout, adder_3_cout;

  Adder #(.width(1)) adder_1 (.a(A1), .b(B1), .out(S1), .cin(Cin), .cout(adder_1_cout));
  Adder #(.width(1)) adder_2 (.a(A2), .b(B2), .out(S2), .cin(adder_1_cout), .cout(adder_2_cout));
  Adder #(.width(1)) adder_3 (.a(A3), .b(B3), .out(S3), .cin(adder_2_cout), .cout(adder_3_cout));
  Adder #(.width(1)) adder_4 (.a(A4), .b(B4), .out(S4), .cin(adder_3_cout), .cout(Cout));
endmodule

module Binary_Adder_Subtractor (
  input  A4,
  input  A3,
  input  A2,
  input  A1,
  input  MODE,
  input  B4,
  input  B3,
  input  B2,
  input  B1,
  output [3:0] OUTPUT,
  output Cout
);

  wire ic_7486_quadruple_2_input_xor_gates_1_out_9, ic_7486_quadruple_2_input_xor_gates_1_out_10,
       ic_7486_quadruple_2_input_xor_gates_1_out_11, ic_7486_quadruple_2_input_xor_gates_1_out_12;

  IC_7486_quadruple_2_input_XOR_gates ic_7486_quadruple_2_input_xor_gates_1 (
    .in_1(MODE), .in_2(B1), .in_3(MODE), .in_4(B2), .in_5(B4), .in_6(MODE), .in_7(B3), .in_8(MODE),
    .out_9(ic_7486_quadruple_2_input_xor_gates_1_out_9),
    .out_10(ic_7486_quadruple_2_input_xor_gates_1_out_10),
    .out_11(ic_7486_quadruple_2_input_xor_gates_1_out_11),
    .out_12(ic_7486_quadruple_2_input_xor_gates_1_out_12));
  IC_74283_4_bit_binary_adder__Vertical ic_74283_4_bit_binary_adder_vertical_1 (
    .Cin(MODE), .A1(A1), .B1(ic_7486_quadruple_2_input_xor_gates_1_out_9), .A2(A2),
    .B2(ic_7486_quadruple_2_input_xor_gates_1_out_10), .A3(A3),
    .B3(ic_7486_quadruple_2_input_xor_gates_1_out_12), .A4(A4),
    .B4(ic_7486_quadruple_2_input_xor_gates_1_out_11), .S1(OUTPUT[0]), .S2(OUTPUT[1]), .S3(OUTPUT[2]),
    .S4(OUTPUT[3]), .Cout(Cout));
endmodule

module IC_74283_4_bit_binary_adder__Horizontal (
  input  Cin,
  input  A1,
  input  B1,
  input  A2,
  input  B2,
  input  A3,
  input  B3,
  input  A4,
  input  B4,
  output S1,
  output S2,
  output S3,
  output S4,
  output Cout
);

  wire adder_1_cout, adder_2_cout, adder_3_cout;

  Adder #(.width(1)) adder_1 (.a(A1), .b(B1), .out(S1), .cin(Cin), .cout(adder_1_cout));
  Adder #(.width(1)) adder_2 (.a(A2), .b(B2), .out(S2), .cin(adder_1_cout), .cout(adder_2_cout));
  Adder #(.width(1)) adder_3 (.a(A3), .b(B3), .out(S3), .cin(adder_2_cout), .cout(adder_3_cout));
  Adder #(.width(1)) adder_4 (.a(A4), .b(B4), .out(S4), .cin(adder_3_cout), .cout(Cout));
endmodule

module BCD_Adder_Circuit (
  input  A4,
  input  A3,
  input  A2,
  input  A1,
  input  B4,
  input  B3,
  input  B2,
  input  B1,
  input  Cin,
  output C__BCD_Carry,
  output Cout__Ignored,
  output [3:0] OUTPUT
);

  wire ic_7408_quadruple_2_input_and_gates_1_out_9, ic_7408_quadruple_2_input_and_gates_1_out_10,
       ic_7432_quadruple_2_input_or_gates_1_out_12, ic_74283_4_bit_binary_adder_horizontal_1_cout,
       ic_74283_4_bit_binary_adder_horizontal_1_s1, ic_74283_4_bit_binary_adder_horizontal_1_s2,
       ic_74283_4_bit_binary_adder_horizontal_1_s3, ic_74283_4_bit_binary_adder_horizontal_1_s4;

  IC_7432_quadruple_2_Input_OR_gates ic_7432_quadruple_2_input_or_gates_1 (
    .in_5(ic_74283_4_bit_binary_adder_horizontal_1_cout), .in_6(ic_7432_quadruple_2_input_or_gates_1_out_12),
    .in_7(ic_7408_quadruple_2_input_and_gates_1_out_10), .in_8(ic_7408_quadruple_2_input_and_gates_1_out_9),
    .out_11(C__BCD_Carry), .out_12(ic_7432_quadruple_2_input_or_gates_1_out_12));  // open: in_1, in_2, in_3, in_4, out_9, out_10
  IC_7408_quadruple_2_Input_AND_gates ic_7408_quadruple_2_input_and_gates_1 (
    .in_1(ic_74283_4_bit_binary_adder_horizontal_1_s2), .in_2(ic_74283_4_bit_binary_adder_horizontal_1_s4),
    .in_3(ic_74283_4_bit_binary_adder_horizontal_1_s3), .in_4(ic_74283_4_bit_binary_adder_horizontal_1_s4),
    .out_9(ic_7408_quadruple_2_input_and_gates_1_out_9), .out_10(ic_7408_quadruple_2_input_and_gates_1_out_10));  // open: in_5, in_6, in_7, in_8, out_11, out_12
  IC_74283_4_bit_binary_adder__Horizontal ic_74283_4_bit_binary_adder_horizontal_1 (
    .Cin(Cin), .A1(A1), .B1(B1), .A2(A2), .B2(B2), .A3(A3), .B3(B3), .A4(A4), .B4(B4),
    .S1(ic_74283_4_bit_binary_adder_horizontal_1_s1), .S2(ic_74283_4_bit_binary_adder_horizontal_1_s2),
    .S3(ic_74283_4_bit_binary_adder_horizontal_1_s3), .S4(ic_74283_4_bit_binary_adder_horizontal_1_s4),
    .Cout(ic_74283_4_bit_binary_adder_horizontal_1_cout));
  IC_74283_4_bit_binary_adder__Horizontal ic_74283_4_bit_binary_adder_horizontal_2 (
    .Cin(Cin), .A1(Cin), .B1(ic_74283_4_bit_binary_adder_horizontal_1_s1), .A2(C__BCD_Carry),
    .B2(ic_74283_4_bit_binary_adder_horizontal_1_s2), .A3(C__BCD_Carry),
    .B3(ic_74283_4_bit_binary_adder_horizontal_1_s3), .A4(Cin),
    .B4(ic_74283_4_bit_binary_adder_horizontal_1_s4), .S1(OUTPUT[0]), .S2(OUTPUT[1]), .S3(OUTPUT[2]),
    .S4(OUTPUT[3]), .Cout(Cout__Ignored));
endmodule
