// Logisim project LAB6(1).circ as structural Verilog: 2 circuits, main circuit main
module main (
  input  S1,
  input  S0,
  input  I0,
  input  I1,
  input  I2,
  input  I3,
  output OUTPUT
);

  wire n2_1_mux_1_out_5, n2_1_mux_2_out_5, not_1_out;

  not not_1 (not_1_out, S0);
  _2_1_mux u_2_1_mux_1 (.in_1(I0), .in_2(I1), .in_3(S1), .in_4(not_1_out), .out_5(n2_1_mux_1_out_5));
  _2_1_mux u_2_1_mux_2 (.in_1(I2), .in_2(I3), .in_3(S1), .in_4(S0), .out_5(n2_1_mux_2_out_5));
  or or_1 (OUTPUT, n2_1_mux_1_out_5, n2_1_mux_2_out_5);
endmodule

module _2_1_mux (
  input  in_1,
  input  in_2,
  input  in_3,
  input  in_4,
  output out_5
);

  Multiplexer multiplexer_1 (.in0(in_1), .in1(in_2), .out(out_5), .sel(in_3), .en(in_4));
endmodule
