// Logisim project LAB6(2).circ as structural Verilog: 2 circuits, main circuit main
module main (
  input  in_1,
  output out_2
);

  IC_74151 ic_74151_1 (
    .I0(1'b1), .I2(in_1), .in_3(in_1), .I3(1'b0), .I4(1'b1), .I5(1'b0), .I6(1'b0), .I7(1'b1), .S0(1'b0),
    .S1(1'b0), .S2(1'b0), .Y(out_2));
endmodule

module IC_74151 (
  input  I0,
  input  I2,
  input  in_3,
  input  I3,
  input  I4,
  input  I5,
  input  I6,
  input  I7,
  input  S0,
  input  S1,
  input  S2,
  output Y
);

  Multiplexer #(.select(3)) multiplexer_1 (
    .in0(I0), .in1(in_3), .in2(I2), .in3(I3), .in4(I4), .in5(I5), .in6(I6), .in7(I7), .out(Y),
    .sel({S2, S1, S0}));  // open: en
endmodule
