// Logisim project BCD to 7 Segment Decoder.circ as structural Verilog: 2 circuits, main circuit main
module main (
  input  [3:0] in_1
);

  wire decoder_ic_1_out_5, decoder_ic_1_out_6, decoder_ic_1_out_7, decoder_ic_1_out_8, decoder_ic_1_out_9,
       decoder_ic_1_out_10, decoder_ic_1_out_11;

  DECODER_IC decoder_ic_1 (
    .out_5(decoder_ic_1_out_5), .out_6(decoder_ic_1_out_6), .out_7(decoder_ic_1_out_7),
    .out_8(decoder_ic_1_out_8), .out_9(decoder_ic_1_out_9), .out_10(decoder_ic_1_out_10),
    .out_11(decoder_ic_1_out_11), .B3(in_1[3]), .B2(in_1[2]), .B1(in_1[1]), .B0(in_1[0]));
  _7_Segment_Display u_7_segment_display_1 (
    .g(decoder_ic_1_out_11), .f(decoder_ic_1_out_10), .a(decoder_ic_1_out_5), .b(decoder_ic_1_out_6),
    .e(decoder_ic_1_out_9), .d(decoder_ic_1_out_8), .c(decoder_ic_1_out_7));  // open: dp
endmodule

module DECODER_IC (
  input  B3,
  input  B2,
  input  B1,
  input  B0,
  output out_5,
  output out_6,
  output out_7,
  output out_8,
  output out_9,
  output out_10,
  output out_11
);

  wire and_1_out, and_2_out, and_3_out, and_4_out, and_5_out, and_6_out, and_7_out, and_8_out, and_9_out,
       and_10_out, and_11_out, not_1_out, not_2_out, not_3_out, not_4_out;

  not not_1 (not_1_out, B3);
  not not_2 (not_2_out, B1);
  not not_3 (not_3_out, B2);
  not not_4 (not_4_out, B0);
  and and_1 (and_1_out, not_4_out, not_3_out);
  and and_2 (and_2_out, B2, B0);
  and and_3 (and_3_out, B0, B1);
  and and_4 (and_4_out, not_4_out, not_2_out);
  and and_5 (and_5_out, B1, not_4_out);
  and and_6 (and_6_out, not_3_out, B1);
  and and_7 (and_7_out, B2, not_2_out, B0);
  and and_8 (and_8_out, B2, not_2_out);
  and and_9 (and_9_out, B2, not_4_out);
  and and_10 (and_10_out, B2, not_2_out);
  and and_11 (and_11_out, not_3_out, B1);
  or or_1 (out_5, and_1_out, B3, B1, and_2_out);
  or or_2 (out_6, and_3_out, B3, not_3_out, and_4_out);
  or or_3 (out_7, B3, B2, not_2_out, B0);
  or or_4 (out_8, and_1_out, B3, and_5_out, and_6_out, and_7_out);
  or or_5 (out_9, and_5_out, and_1_out);
  or or_6 (out_10, and_4_out, B3, and_8_out, and_9_out);
  or or_7 (out_11, B3, and_5_out, and_10_out, and_11_out);
endmodule
